# Fritzing sketch SelectBulbWithButtons (saved by Fritzing 0.9.3b)
breadboards: 1

parts:
  Part1 = Arduino Uno (Rev3)
  1 = Pushbutton [package="[THT]"]
  2 = Pushbutton [package="[THT]"]
  4 = Pushbutton [package="[THT]"]
  8 = Pushbutton [package="[THT]"]
  SEND = Pushbutton [package="[THT]"]
  R1 = Resistor [tolerance=±5% resistance=220 package=THT]
  R2 = Resistor [tolerance=±5% resistance=220 package=THT]
  R3 = Resistor [tolerance=±5% resistance=220 package=THT]
  R4 = Resistor [tolerance=±5% resistance=220 package=THT]
  R5 = Resistor [tolerance=±5% resistance=220 package=THT]
  U1 = 74HC595 [package="DIP16 [THT]"]
  LED1 = LED - 5mm [color="Red (633nm)" package="5 mm [THT]"]
  LED2 = LED - 5mm [color="Red (633nm)" package="5 mm [THT]"]
  LED3 = LED - 5mm [color="Red (633nm)" package="5 mm [THT]"]
  LED4 = LED - 5mm [color="Red (633nm)" package="5 mm [THT]"]
  LED5 = LED - 5mm [color="Red (633nm)" package="5 mm [THT]"]
  LED6 = LED - 5mm [color="Red (633nm)" package="5 mm [THT]"]
  LED7 = LED - 5mm [color="Red (633nm)" package="5 mm [THT]"]
  LED8 = LED - 5mm [color="Red (633nm)" package="5 mm [THT]"]
  R7 = Resistor [tolerance=±5% resistance=220 package=THT]
  R8 = Resistor [tolerance=±5% resistance=220 package=THT]
  R9 = Resistor [tolerance=±5% resistance=220 package=THT]
  R10 = Resistor [tolerance=±5% resistance=220 package=THT]
  R11 = Resistor [tolerance=±5% resistance=220 package=THT]
  R12 = Resistor [tolerance=±5% resistance=220 package=THT]
  R13 = Resistor [tolerance=±5% resistance=220 package=THT]
  R14 = Resistor [tolerance=±5% resistance=220 package=THT]

nets:
  N1: Part1.D8, U1.ST_CP
  N2: Part1.D9_PWM, 4.Pin_3, 4.Pin_4, R3.Pin_1
  N3: Part1.D10_PWM/SS, 2.Pin_3, 2.Pin_4, R4.Pin_1
  N4: Part1.D11_PWM/MOSI, U1.DS
  N5: Part1.D12/MISO, U1.SH_CP
  N6: Part1.D13/SCK, 1.Pin_3, 1.Pin_4, R5.Pin_1
  N7: Part1.D6_PWM, SEND.Pin_3, SEND.Pin_4, R1.Pin_1
  N8: Part1.D7, 8.Pin_3, 8.Pin_4, R2.Pin_1
  5V: Part1.5V, 1.Pin_1, 1.Pin_2, 2.Pin_1, 2.Pin_2, 4.Pin_1, 4.Pin_2, 8.Pin_1, 8.Pin_2, SEND.Pin_1, SEND.Pin_2, U1.MR, U1.VCC
  GND: Part1.GND, R1.Pin_0, R2.Pin_0, R3.Pin_0, R4.Pin_0, R5.Pin_0, U1.GND, U1.OE, LED1.cathode, LED2.cathode, LED3.cathode, LED4.cathode, LED5.cathode, LED6.cathode, LED7.cathode, LED8.cathode
  N9: U1.Q1, R14.Pin_1
  N10: U1.Q2, R13.Pin_1
  N11: U1.Q3, R12.Pin_1
  N12: U1.Q4, R11.Pin_1
  N13: U1.Q5, R10.Pin_1
  N14: U1.Q6, R9.Pin_1
  N15: U1.Q7, R8.Pin_1
  N16: U1.Q0, R7.Pin_1
  N17: LED1.anode, R7.Pin_0
  N18: LED2.anode, R14.Pin_0
  N19: LED3.anode, R13.Pin_0
  N20: LED4.anode, R12.Pin_0
  N21: LED5.anode, R11.Pin_0
  N22: LED6.anode, R10.Pin_0
  N23: LED7.anode, R9.Pin_0
  N24: LED8.anode, R8.Pin_0

// code stored in the sketch: SelectBulbWithButtons.ino
/*Enter a number in binary in range(0-8) to light one of the diode */


int latchPin = 8;
int clockPin = 12;
int dataPin = 11;

const int bp1 = 13;
const int bp2 = 10;
const int bp3 = 9;
const int bp4 = 7;
const int bp5 = 6;



int bNum;

void setup() {
  Serial.begin(9600);
  pinMode(latchPin, OUTPUT);
  pinMode(clockPin, OUTPUT);
  pinMode(dataPin, OUTPUT);

  pinMode(bp1, INPUT);
  pinMode(bp2, INPUT);
  pinMode(bp3, INPUT);
  pinMode(bp4, INPUT);
  pinMode(bp5, INPUT);

}

void loop() {
  bNum = 0;
  int buttonState1 = 0;
  int buttonState2 = 0;
  int buttonState3 = 0;
  int buttonState4 = 0;
  
  while (digitalRead(bp5) == LOW) {
    if (buttonState1 == 0) {
      buttonState1 = digitalRead(bp1);
    }
    if (buttonState2 == 0) {
      buttonState2 = digitalRead(bp2);
    }
    if (buttonState3 == 0) {
      buttonState3 = digitalRead(bp3);
    }
    if (buttonState4 == 0) {
      buttonState4 = digitalRead(bp4);
    }

  }
  if (buttonState1 == HIGH) {
    bNum = bNum + 1;
  } 
  if (buttonState2 == HIGH) {
    bNum = bNum + 2;
  } 
  if (buttonState3 == HIGH) {
    bNum = bNum + pow(2, 2);
  } 
  if (buttonState4 == HIGH) {
    bNum = bNum + pow(2, 3);
  }
    

  Serial.print(bNum);

  if (bNum > 8) {
    Serial.print("Enter a new number.");
    loop();
  }

    digitalWrite(latchPin, 0);
    if (bNum==0){
      shiftOut(dataPin, clockPin, LSBFIRST, 0x00);
      
    }else{
      shiftOut(dataPin, clockPin, LSBFIRST, 1<<bNum-1); 
      
    }
    digitalWrite(latchPin, 1);
    
    delay(500);


}
